// Logisim project Jumping-plan.circ as structural Verilog: 1 circuit, main circuit main
module main (
);

  wire and_1_out, and_2_out, and_3_out, and_4_out, button_1_out, clock_1_out, j_k_ff_1_q, not_1_out,
       not_2_out, not_3_out, or_1_out, or_2_out, or_3_out, undriven;
  wire [2:0] counter_1_q;

  or or_1 (or_1_out, undriven, and_1_out);
  Button button_1 (.out(button_1_out));
  Clock clock_1 (.out(clock_1_out));
  J_K_Flip_Flop j_k_ff_1 (
    .J(1'b1), .clk(button_1_out), .K(1'b1), .Q(j_k_ff_1_q), .reset(or_2_out));  // open: Qn, preset, en
  not not_1 (not_1_out, button_1_out);
  Counter #(.width(3), .max('h7)) counter_1 (
    .Q(counter_1_q), .clk(and_1_out), .clr(or_3_out));  // open: load, D, count, carry
  and and_1 (and_1_out, clock_1_out, j_k_ff_1_q);
  or or_2 (or_2_out, and_2_out, and_4_out);
  and and_2 (and_2_out, not_1_out, and_3_out);
  not not_2 (not_2_out, counter_1_q[1]);
  or or_3 (or_3_out, and_4_out, or_2_out);
  and and_3 (and_3_out, counter_1_q[0], counter_1_q[1], not_3_out);
  not not_3 (not_3_out, counter_1_q[2]);
  and and_4 (and_4_out, counter_1_q[0], not_2_out, counter_1_q[2]);

  // Notes on the sheet:
  //   Falling Down Logic
  //   (is dino NOT on ground * is dino NOT jumping * a clock)
  //   Shift values in Register
  //   (RIGHT SHIFT when not lit)
  //   Set Directional Shift Register to LEFT SHIFT
endmodule
